// Logisim project FA.circ as structural Verilog
module HalfAdder (
  input  A,
  input  B,
  output Sum,
  output Cout
);

  // _7408 7408_1: pin names not known; wires that end beside it: A, B, Cout, 1'b0, 1'b1
  // _7486 7486_1: pin names not known; wires that end beside it: A, B, Sum, 1'b0, 1'b1
endmodule

module FullAdder (
  input  A,
  input  B,
  input  Cin,
  output Cout,
  output Sum
);

  wire halfadder_1_cout, halfadder_1_sum, halfadder_2_cout;

  HalfAdder halfadder_1 (.A(A), .B(B), .Sum(halfadder_1_sum), .Cout(halfadder_1_cout));
  HalfAdder halfadder_2 (.A(halfadder_1_sum), .B(Cin), .Sum(Sum), .Cout(halfadder_2_cout));
  or or_1 (Cout, halfadder_1_cout, halfadder_2_cout);
endmodule
