// Logisim project ALU subcircuit.circ as structural Verilog: 1 circuit, main circuit ALU subcircuit
module ALU_subcircuit (
  input  in_1,
  input  in_2,
  input  in_3,
  input  in_4,
  input  in_5,
  input  in_6,
  input  [1:0] in_7
);

  wire _7447_p5, _7447_p6, _7447_p7, _7447_p8, _7447_p9, _7447_p10, _7447_p11, alu_1_out_13, alu_1_out_14,
       alu_1_r1, alu_1_r2, alu_1_r3, alu_1_r4, alu_1_sr, alu_1_zero_flag;

  ALU alu_1 (
    .in_7(in_7), .SA(in_1), .A1(in_2), .A2(in_3), .SB(in_4), .B1(in_5), .B2(in_6), .SR(alu_1_sr),
    .R1(alu_1_r1), .R2(alu_1_r2), .R3(alu_1_r3), .R4(alu_1_r4), .out_13(alu_1_out_13),
    .zero_flag(alu_1_zero_flag), .out_14(alu_1_out_14));
  LED led_1 (.in(alu_1_out_13));
  LED led_2 (.in(alu_1_zero_flag));
  // Simple_buzzer simple_buzzer_1: pin names not known; wires that end beside it: alu_1_out_14, 1'b0
  // _7_segment_display_driver _7447: pin names not known; wires that end beside it: alu_1_r1, alu_1_r2, alu_1_r3, alu_1_r4, _7447_p5, _7447_p6, _7447_p7, _7447_p8, _7447_p9, _7447_p10, _7447_p11
  _7_Segment_Display u_7_segment_display_1 (.g(alu_1_sr));  // open: f, a, b, e, d, c, dp
  _7_Segment_Display u_7_segment_display_2 (
    .g(_7447_p11), .f(_7447_p10), .a(_7447_p5), .b(_7447_p6), .e(_7447_p9), .d(_7447_p8), .c(_7447_p7));  // open: dp

  // Notes on the sheet:
  //   00 Add
  //   01 Sub
  //   10 Mult.
  //   11 Rem
  //   Negative flag
  //   zero flag
  //   Divide by zero Buzzer
endmodule
