// Logisim project ALU-edited (1).circ as structural Verilog: 1 circuit, main circuit ALU
module ALU (
  input  SA,
  input  A1,
  input  A2,
  input  SB,
  input  B1,
  input  B2,
  input  [1:0] in_7,
  output R1,
  output R2,
  output R3,
  output R4,
  output SR,
  output out_13,
  output out_14,
  output zero_flag
);

  wire main_1_r1, main_1_r2, main_1_r3, main_1_sign_bit, main_2_r1, main_2_r2, main_2_r3, main_2_r4,
       main_2_rs, multiplexer_1_out, n7402_1_p1, n7402_1_p4, n7486_1_p2, remaindercircuit_1_out_10,
       remaindercircuit_1_r1, remaindercircuit_1_r2, remaindercircuit_1_rs;

  adder_subtracter_circuit__2__main main_1 (
    .a1(A1), .b1(B1), .a2(A2), .b2(B2), .sign_A(in_7[0]), .sign_B(SB), .sign_bit(main_1_sign_bit),
    .r1(main_1_r1), .r2(main_1_r2), .r3(main_1_r3), .op(SA));
  Multiplexer #(.select(2), .enable("false")) multiplexer_1 (
    .in0(main_1_sign_bit), .in1(main_1_sign_bit), .in2(main_2_r1), .in3(remaindercircuit_1_rs),
    .out(multiplexer_1_out), .sel(in_7));
  // _7486 7486_1: pin names not known; wires that end beside it: multiplexer_1_out, n7486_1_p2, out_13
  multiplier_main main_2 (
    .AS(SA), .BS(SB), .A2(A2), .A1(A1), .B2(B2), .B1(B1), .R4(main_2_r4), .R3(main_2_r3), .R2(main_2_r2),
    .RS(main_2_rs), .R1(main_2_r1));
  Multiplexer #(.select(2), .enable("false")) multiplexer_2 (
    .in0(1'b0), .in1(1'b0), .in2(main_2_rs), .in3(1'b0), .out(R1), .sel(in_7));
  // _7402 7402_1: pin names not known; wires that end beside it: n7402_1_p1, R1, R2, n7402_1_p4, R3, R4
  // _7408 7408_1: pin names not known; wires that end beside it: n7402_1_p1, n7402_1_p4, zero_flag, zero_flag, multiplexer_1_out, n7486_1_p2
  Multiplexer #(.select(2), .enable("false")) multiplexer_3 (
    .in0(main_1_r1), .in1(main_1_r1), .in2(main_2_r2), .in3(1'b0), .out(R2), .sel(in_7));
  Multiplexer #(.select(2), .enable("false")) multiplexer_4 (
    .in0(main_1_r2), .in1(main_1_r2), .in2(main_2_r3), .in3(remaindercircuit_1_r1), .out(R3), .sel(in_7));
  RemainderCircuit remaindercircuit_1 (
    .sign_A0(SA), .A1(A1), .A2(A2), .sign_B0(SB), .B1(B1), .B2(B2), .RS(remaindercircuit_1_rs),
    .R1(remaindercircuit_1_r1), .R2(remaindercircuit_1_r2), .out_10(remaindercircuit_1_out_10));
  Multiplexer #(.select(2), .enable("false")) multiplexer_5 (
    .in0(main_1_r3), .in1(main_1_r3), .in2(main_2_r4), .in3(remaindercircuit_1_r2), .out(R4), .sel(in_7));
  Multiplexer #(.select(2), .enable("false")) multiplexer_6 (
    .in0(1'b0), .in1(1'b0), .in2(1'b0), .in3(remaindercircuit_1_out_10), .out(out_14), .sel(in_7));

  assign SR = out_13;

  // Notes on the sheet:
  //   Negative flag
  //   Divide By zero flag
endmodule
