// Logisim project Remainder_circuit (1).circ as structural Verilog: 1 circuit, main circuit RemainderCircuit
module RemainderCircuit (
  input  sign_A0,
  input  A1,
  input  A2,
  input  sign_B0,
  input  B1,
  input  B2,
  output RS,
  output R1,
  output R2,
  output out_10
);

  wire n7404_1_p2, n7404_1_p4, n7404_1_p9, n7404_1_p11, n7408_1_p3, n7408_1_p6, n7408_1_p11, n7408_1_p14,
       n7408_2_p3, n7408_2_p11;

  // _7404 7404_1: pin names not known; wires that end beside it: A2, n7404_1_p2, A1, n7404_1_p4, 1'b0, sign_B0, 1'b1, B1, n7404_1_p9, B2, n7404_1_p11
  // _7408 7408_1: pin names not known; wires that end beside it: B1, A2, n7408_1_p3, n7408_1_p3, n7404_1_p4, n7408_1_p6, 1'b0, 1'b1, n7404_1_p11, B1, n7408_1_p11, n7408_1_p11, A2, n7408_1_p14
  // _7408 7408_2: pin names not known; wires that end beside it: n7404_1_p2, A1, n7408_2_p3, n7404_1_p9, n7404_1_p11, out_10, 1'b0, 1'b1, B1, B2, n7408_2_p11, n7408_2_p11, n7408_2_p3, R1
  // _7432 7432_1: pin names not known; wires that end beside it: n7408_1_p14, n7408_1_p6, R2, 1'b0, 1'b1

  assign RS = sign_A0;

  // Notes on the sheet:
  //   Divide by zero flag
endmodule
