// Logisim project adder-subtracter circuit (2).circ as structural Verilog: 1 circuit, main circuit main
module main (
  input  op,
  input  sign_A,
  input  sign_B,
  input  a1,
  input  b1,
  input  a2,
  input  b2,
  output sign_bit,
  output r1,
  output r2,
  output r3
);

  wire fulladder_1_sum, fulladder_2_cout, n7402_1_p4, n7404_1_p1, n7404_1_p2, n7404_1_p3, n7404_1_p4,
       n7404_1_p5, n7404_1_p6, n7408_1_p2, n7408_1_p3, n7408_1_p4, n7408_1_p6, n7486_1_p3, n7486_2_p6,
       n7486_2_p9;

  LED led_1 (.in(sign_bit));
  // _7404 7404_1: pin names not known; wires that end beside it: n7404_1_p1, n7404_1_p2, n7404_1_p3, n7404_1_p4, n7404_1_p5, n7404_1_p6
  // _7408 7408_1: pin names not known; wires that end beside it: n7404_1_p1, n7408_1_p2, n7408_1_p3, n7408_1_p4, n7404_1_p6, n7408_1_p6, n7404_1_p2, n7408_1_p2, r1, n7404_1_p1, r3, n7408_1_p4
  FullAdder fulladder_1 (.A(fulladder_2_cout), .B(n7486_2_p9), .Cin(a1), .Cout(n7404_1_p5), .Sum(fulladder_1_sum));
  FullAdder fulladder_2 (.A(n7404_1_p1), .B(n7486_2_p6), .Cin(a2), .Cout(fulladder_2_cout), .Sum(r3));
  // _7402 7402_1: pin names not known; wires that end beside it: n7404_1_p3, r1, r3, n7402_1_p4, n7404_1_p4, r2
  // _7486 7486_1: pin names not known; wires that end beside it: sign_B, op, n7486_1_p3, n7404_1_p1, n7404_1_p5, n7408_1_p2, op, n7408_1_p3, sign_bit
  // _7486 7486_2: pin names not known; wires that end beside it: n7486_1_p3, sign_A, n7404_1_p1, n7404_1_p1, b2, n7486_2_p6, b1, n7404_1_p1, n7486_2_p9, n7408_1_p6, fulladder_1_sum, r2
  LED led_2 (.in(n7402_1_p4));

  // Notes on the sheet:
  //   negative flag
  //   zero flag
endmodule
