// Logisim project multiplier.circ as structural Verilog: 1 circuit, main circuit main
module main (
  input  AS,
  input  BS,
  input  A2,
  input  A1,
  input  B2,
  input  B1,
  output RS,
  output R2,
  output R3,
  output R4,
  output R1
);

  wire n7408_1_p6, n7408_1_p11, n7408_1_p14, n7486_1_p8;

  // _7408 7408_1: pin names not known; wires that end beside it: A2, B2, R4, A1, B2, n7408_1_p6, 1'b1, 1'b0, A2, B1, n7408_1_p11, A1, B1, n7408_1_p14
  // _7486 7486_1: pin names not known; wires that end beside it: n7408_1_p11, n7408_1_p6, R3, BS, AS, R1, 1'b1, n7486_1_p8, n7408_1_p14, R2
  // _7408 7408_2: pin names not known; wires that end beside it: 1'b1, n7408_1_p11, n7408_1_p6, n7486_1_p8, n7486_1_p8, n7408_1_p14, RS, 1'b0, 1'b1
endmodule
